# Fritzing sketch LCD_schematic (saved by Fritzing 1.0.3b)
breadboards: 1

parts:
  Part1 = Arduino Uno (Rev3) - ICSP
  LCD1 = Waveshare 1.28 inch Round 240x240 LCD Display

nets:
  N1: Part1.D8, LCD1.pin_7
  N2: Part1.D9_PWM, LCD1.pin_8
  N3: Part1.D10_PWM/SS, LCD1.pin_5
  N4: Part1.D11_PWM/MOSI, LCD1.pin3
  N5: Part1.D13/SCK, LCD1.pin4
  N6: Part1.D7, LCD1.pin_6
  N7: Part1.5V, LCD1.pin_1
  N8: Part1.GND, LCD1.pin2

custom parts:
  Waveshare 1.28 inch Round 240x240 LCD Display: Waveshare 1.28 inch Round 240x240 LCD Display with GC9A01 Controller
