# Fritzing sketch MPU6050 (saved by Fritzing 1.0.3b)

parts:
  Part1 = Arduino Uno (Rev3) - ICSP
  Part2 = InvenSense MPU6050

nets:
  N1: Part1.A4/SDA, Part2.SDA
  N2: Part1.A5/SCL, Part2.SCL
  GND: Part1.GND, Part2.GND
  N3: Part1.D2, Part2.INT
  5V: Part1.5V, Part2.VCC
