# Fritzing sketch TFT+Arduino (saved by Fritzing 1.0.3b)
breadboards: 1

parts:
  LCD1 = TFT 1.8 inch 160x128 w SD
  Part1 = Arduino Uno (Rev3) - ICSP

nets:
  N1: LCD1.pin_1, Part1.5V
  N2: LCD1.pin2, Part1.GND
  N3: LCD1.pin3, Part1.D10_PWM/SS
  N4: LCD1.pin4, Part1.D8
  N5: LCD1.pin_5, Part1.D9_PWM
  N6: LCD1.pin_6, Part1.D11_PWM/MOSI
  N7: LCD1.pin_7, Part1.D13/SCK
  N8: LCD1.pin_8, Part1.3V3

custom parts:
  TFT 1.8 inch 160x128 w SD: This is a generic 1.8 tft spi lcd display available on ebay and others. The 1.8" display has 128x160 color pixels.
